// Logisim project LATCH D COM CLOCK.circ as structural Verilog: 1 circuit, main circuit main
module main (
  input  D,
  input  Clock,
  output NQ,
  output Q
);

  wire and_1_out, and_2_out, not_1_out;

  not not_1 (not_1_out, D);
  and and_1 (and_1_out, D, Clock);
  and and_2 (and_2_out, Clock, not_1_out);
  nor nor_1 (NQ, and_1_out, Q);
  nor nor_2 (Q, NQ, and_2_out);

  // Notes on the sheet:
  //   LATCH D com Clock
endmodule
