// Logisim project Memória_Rom,q26.circ as structural Verilog: 1 circuit, main circuit main
module main (
  input  A0,
  input  A1,
  input  A2,
  output S0
);

  wire and_2_out, and_3_out, and_4_out, not_1_out, not_2_out, not_3_out, not_4_out, not_5_out;

  not not_1 (not_1_out, A0);
  // AND_Gate and_1 has open pins: in4=not_1_out, out=open
  and and_2 (and_2_out, A1, A1, A0);
  not not_2 (not_2_out, A0);
  not not_3 (not_3_out, A1);
  not not_4 (not_4_out, A2);
  and and_3 (and_3_out, A2, not_3_out, not_2_out);
  or or_1 (S0, and_2_out, and_3_out, and_4_out);
  not not_5 (not_5_out, A1);
  and and_4 (and_4_out, not_4_out, not_5_out, A0);
endmodule
