// Logisim project OULTIMOTRABALHO.circ as structural Verilog: 3 circuits, main circuit main
module main (
  input  Cin,
  input  A0,
  input  A1,
  input  A2,
  input  A3,
  input  S0,
  input  B0,
  input  S1,
  input  B1,
  input  B2,
  input  B3,
  input  CIN_2,
  input  in_13,
  input  in_14,
  input  in_15,
  input  in_16,
  input  Complemento_de_1,
  output A0_2,
  output A1_2,
  output A2_2,
  output A3_2
);

  wire Clock_2_out, Clock_out, paralelo_paralelo_1_q0, paralelo_paralelo_1_q1, paralelo_paralelo_1_q2,
       paralelo_paralelo_1_q3, paralelo_paralelo_2_q0, paralelo_paralelo_2_q1, paralelo_paralelo_2_q2,
       paralelo_paralelo_2_q3;
  wire [3:0] and_1_out_9, not_1_out, somador_4_bits_1_s0, subtrator_1_s0;

  Clock Clock (.out(Clock_out));
  Clock Clock_2 (.out(Clock_2_out));
  paralelo_paralelo paralelo_paralelo_1 (
    .D0(A0), .D1(A1), .D2(A2), .D3(A3), .Clock(Clock_out), .Q0(paralelo_paralelo_1_q0),
    .Q1(paralelo_paralelo_1_q1), .Q2(paralelo_paralelo_1_q2), .Q3(paralelo_paralelo_1_q3));
  paralelo_paralelo paralelo_paralelo_2 (
    .D0(B0), .D1(B1), .D2(B2), .D3(B3), .Clock(Clock_2_out), .Q0(paralelo_paralelo_2_q0),
    .Q1(paralelo_paralelo_2_q1), .Q2(paralelo_paralelo_2_q2), .Q3(paralelo_paralelo_2_q3));
  Somador_4_bits somador_4_bits_1 (
    .A0(paralelo_paralelo_1_q0), .B0(paralelo_paralelo_2_q0), .A1(paralelo_paralelo_1_q1),
    .B1(paralelo_paralelo_2_q1), .A2(paralelo_paralelo_1_q2), .B2(paralelo_paralelo_2_q2),
    .A3(paralelo_paralelo_1_q3), .B3(paralelo_paralelo_2_q3), .Cin(Cin), .S0(somador_4_bits_1_s0[0]),
    .S1(somador_4_bits_1_s0[1]), .S2(somador_4_bits_1_s0[2]), .S3(somador_4_bits_1_s0[3]));  // open: Cout
  \and  and_1 (
    .A0(paralelo_paralelo_1_q0), .B0(paralelo_paralelo_2_q0), .A1(paralelo_paralelo_1_q1),
    .B1(paralelo_paralelo_2_q1), .A2(paralelo_paralelo_1_q2), .B2(paralelo_paralelo_2_q2),
    .A3(paralelo_paralelo_1_q3), .B3(paralelo_paralelo_2_q3), .out_9(and_1_out_9[0]),
    .out_10(and_1_out_9[1]), .out_11(and_1_out_9[2]), .out_12(and_1_out_9[3]));
  not not_1 (not_1_out[0], paralelo_paralelo_1_q0);
  not not_2 (not_1_out[1], paralelo_paralelo_1_q1);
  not not_3 (not_1_out[2], paralelo_paralelo_1_q2);
  not not_4 (not_1_out[3], paralelo_paralelo_1_q3);
  Subtrator subtrator_1 (
    .in_1(Complemento_de_1), .in_10(in_16), .in_11(in_15), .in_12(in_14), .in_13(in_13),
    .B3(paralelo_paralelo_2_q3), .B2(paralelo_paralelo_2_q2), .B1(paralelo_paralelo_2_q1),
    .B0(paralelo_paralelo_2_q0), .A3(paralelo_paralelo_1_q3), .A2(paralelo_paralelo_1_q2),
    .A1(paralelo_paralelo_1_q1), .A0(paralelo_paralelo_1_q0), .S3(subtrator_1_s0[3]), .S2(subtrator_1_s0[2]),
    .S1(subtrator_1_s0[1]), .S0(subtrator_1_s0[0]), .Cin(CIN_2));  // open: out_15
  Multiplexer #(.select(2), .width(4)) multiplexer_1 (
    .in0(somador_4_bits_1_s0), .in1(and_1_out_9), .in2(not_1_out), .in3(subtrator_1_s0),
    .out({A3_2, A2_2, A1_2, A0_2}), .sel({S1, S0}));  // open: en

  // Notes on the sheet:
  //   Entradas
  //   AND
  //   Somador
  //   NOT
  //   Subtrator
  //   Seletor de operações
  //   Saídas
endmodule

module \and  (
  input  A0,
  input  B0,
  input  A1,
  input  B1,
  input  A2,
  input  B2,
  input  A3,
  input  B3,
  output out_9,
  output out_10,
  output out_11,
  output out_12
);

  and and_1 (out_9, A0, B0);
  and and_2 (out_11, A2, B2);
  and and_3 (out_12, A3, B3);
  and and_4 (out_10, A1, B1);
endmodule

module Com_led (
  input  A0,
  input  A1,
  input  A2,
  input  A3,
  input  S0,
  input  B0,
  input  S1,
  input  B1,
  input  S2,
  input  B2,
  input  B3,
  input  Preset,
  input  Enable,
  input  Clear
);

  wire clock_1_out, clock_2_out, Clock_3_out, paralelo_paralelo_1_q0, paralelo_paralelo_1_q1,
       paralelo_paralelo_1_q2, paralelo_paralelo_1_q3, paralelo_paralelo_2_q0, paralelo_paralelo_2_q1,
       paralelo_paralelo_2_q2, paralelo_paralelo_2_q3, tarefa01_1_a, tarefa01_1_a0, tarefa01_1_b,
       tarefa01_1_b0, tarefa01_1_c, tarefa01_1_c0, tarefa01_1_d, tarefa01_1_d0, tarefa01_1_e, tarefa01_1_e0,
       tarefa01_1_f, tarefa01_1_f0, tarefa01_1_g, tarefa01_1_g0;
  wire [3:0] and_1_out_9, contador_de_6_bits_1_q0, multiplexer_1_out, multiplexer_2_out, not_1_out,
       somador_4_bits_1_s0, subtrator_1_s0;

  Clock clock_1 (.out(clock_1_out));
  Clock clock_2 (.out(clock_2_out));
  paralelo_paralelo paralelo_paralelo_1 (
    .D0(A0), .D1(A1), .D2(A2), .D3(A3), .Clock(clock_1_out), .Q0(paralelo_paralelo_1_q0),
    .Q1(paralelo_paralelo_1_q1), .Q2(paralelo_paralelo_1_q2), .Q3(paralelo_paralelo_1_q3));
  paralelo_paralelo paralelo_paralelo_2 (
    .D0(B0), .D1(B1), .D2(B2), .D3(B3), .Clock(clock_2_out), .Q0(paralelo_paralelo_2_q0),
    .Q1(paralelo_paralelo_2_q1), .Q2(paralelo_paralelo_2_q2), .Q3(paralelo_paralelo_2_q3));
  Clock Clock_3 (.out(Clock_3_out));
  Somador_4_bits somador_4_bits_1 (
    .A0(paralelo_paralelo_1_q0), .B0(paralelo_paralelo_2_q0), .A1(paralelo_paralelo_1_q1),
    .B1(paralelo_paralelo_2_q1), .A2(paralelo_paralelo_1_q2), .B2(paralelo_paralelo_2_q2),
    .A3(paralelo_paralelo_1_q3), .B3(paralelo_paralelo_2_q3), .Cin(1'b0), .S0(somador_4_bits_1_s0[0]),
    .S1(somador_4_bits_1_s0[1]), .S2(somador_4_bits_1_s0[2]), .S3(somador_4_bits_1_s0[3]));  // open: Cout
  \and  and_1 (
    .A0(paralelo_paralelo_1_q0), .B0(paralelo_paralelo_2_q0), .A1(paralelo_paralelo_1_q1),
    .B1(paralelo_paralelo_2_q1), .A2(paralelo_paralelo_1_q2), .B2(paralelo_paralelo_2_q2),
    .A3(paralelo_paralelo_1_q3), .B3(paralelo_paralelo_2_q3), .out_9(and_1_out_9[0]),
    .out_10(and_1_out_9[1]), .out_11(and_1_out_9[2]), .out_12(and_1_out_9[3]));
  not not_1 (not_1_out[0], paralelo_paralelo_1_q0);
  not not_2 (not_1_out[1], paralelo_paralelo_1_q1);
  not not_3 (not_1_out[2], paralelo_paralelo_1_q2);
  not not_4 (not_1_out[3], paralelo_paralelo_1_q3);
  Subtrator subtrator_1 (
    .in_1(1'b1), .in_10(1'b0), .in_11(1'b0), .in_12(1'b0), .in_13(1'b0), .B3(paralelo_paralelo_2_q3),
    .B2(paralelo_paralelo_2_q2), .B1(paralelo_paralelo_2_q1), .B0(paralelo_paralelo_2_q0),
    .A3(paralelo_paralelo_1_q3), .A2(paralelo_paralelo_1_q2), .A1(paralelo_paralelo_1_q1),
    .A0(paralelo_paralelo_1_q0), .S3(subtrator_1_s0[3]), .S2(subtrator_1_s0[2]), .S1(subtrator_1_s0[1]),
    .S0(subtrator_1_s0[0]), .Cin(1'b1));  // open: out_15
  Contador_de_6_bits contador_de_6_bits_1 (
    .Clock(Clock_3_out), .Preset(Preset), .Enable(Enable), .Clear(Clear), .Q3(contador_de_6_bits_1_q0[3]),
    .Q2(contador_de_6_bits_1_q0[2]), .Q1(contador_de_6_bits_1_q0[1]), .Q0(contador_de_6_bits_1_q0[0]));  // open: Q5, Q4
  Multiplexer #(.select(3), .width(4)) multiplexer_1 (
    .in0(somador_4_bits_1_s0), .in3(subtrator_1_s0), .in4(contador_de_6_bits_1_q0), .out(multiplexer_1_out),
    .sel({S2, S1, S0}));  // open: in1, in2, in5, in6, in7, en
  Multiplexer #(.select(3), .width(4)) multiplexer_2 (
    .in1(and_1_out_9), .in2(not_1_out), .out(multiplexer_2_out), .sel({S2, S1, S0}));  // open: in0, in3, in4, in5, in6, in7, en
  LED led_1 (.in(multiplexer_2_out[0]));
  LED led_2 (.in(multiplexer_2_out[1]));
  LED led_3 (.in(multiplexer_2_out[2]));
  LED led_4 (.in(multiplexer_2_out[3]));
  tarefa01 tarefa01_1 (
    .S4(1'b0), .S3(multiplexer_1_out[3]), .S2(multiplexer_1_out[2]), .S1(multiplexer_1_out[1]),
    .S0(multiplexer_1_out[0]), .in_6(1'b0), .in_7(1'b0), .b(tarefa01_1_b), .a(tarefa01_1_a),
    .f(tarefa01_1_f), .g(tarefa01_1_g), .e(tarefa01_1_e), .d(tarefa01_1_d), .c(tarefa01_1_c),
    .b0(tarefa01_1_b0), .a0(tarefa01_1_a0), .f0(tarefa01_1_f0), .g0(tarefa01_1_g0), .e0(tarefa01_1_e0),
    .d0(tarefa01_1_d0), .c0(tarefa01_1_c0));
  _7_Segment_Display u_7_segment_display_1 (
    .g(tarefa01_1_g0), .f(tarefa01_1_f0), .a(tarefa01_1_a0), .b(tarefa01_1_b0), .e(tarefa01_1_e0),
    .d(tarefa01_1_d0), .c(tarefa01_1_c0));  // open: dp
  _7_Segment_Display u_7_segment_display_2 (
    .g(tarefa01_1_g), .f(tarefa01_1_f), .a(tarefa01_1_a), .b(tarefa01_1_b), .e(tarefa01_1_e),
    .d(tarefa01_1_d), .c(tarefa01_1_c));  // open: dp

  // Notes on the sheet:
  //   Entradas
  //   AND
  //   Somador
  //   NOT
  //   Subtrator
  //   Contador
  //   Soma, Subtração e Contador
  //   AND e NOT
endmodule
