// Logisim project circuito combinacional de 4 fios.circ as structural Verilog: 1 circuit, main circuit main
module main (
  input  A,
  input  B,
  output S0,
  output S1,
  output S2,
  output S3
);

  wire not_1_out, not_2_out;

  not not_1 (not_1_out, A);
  not not_2 (not_2_out, B);
  or or_1 (S0, B, A);
  or or_2 (S1, not_1_out, B);
  or or_3 (S2, A, not_2_out);
  or or_4 (S3, not_1_out, not_2_out);

  // Notes on the sheet:
  //   Circuito Combinacional de 4 fios
endmodule
