// Logisim project estudo de multiplexdores.circ as structural Verilog: 1 circuit, main circuit main
// ABCD
module main (
  input  in_1,
  input  in_2,
  input  A,
  input  _00,
  input  _01,
  input  _10,
  input  _11,
  input  [1:0] in_8,
  input  _00_2,
  input  _01_2,
  input  _10_2,
  input  _11_2,
  input  [1:0] in_13,
  input  _00_3,
  input  _01_3,
  input  _10_3,
  input  _11_3,
  input  [1:0] in_18,
  input  _00_4,
  input  _01_4,
  input  _10_4,
  input  _11_4,
  input  [1:0] in_23,
  output S,
  output out_25,
  output out_26,
  output out_27,
  output out_28
);

  Multiplexer multiplexer_1 (.in0(in_1), .in1(in_2), .out(S), .sel(A));  // open: en
  Multiplexer #(.select(2)) multiplexer_2 (
    .in0(_00), .in1(_01), .in2(_10), .in3(_11), .out(out_25), .sel(in_8));  // open: en
  Multiplexer #(.select(2)) multiplexer_3 (
    .in0(_00_2), .in1(_01_2), .in2(_10_2), .in3(_11_2), .out(out_26), .sel(in_13));  // open: en
  Multiplexer #(.select(2)) multiplexer_4 (
    .in0(_00_3), .in1(_01_3), .in2(_10_3), .in3(_11_3), .out(out_27), .sel(in_18));  // open: en
  Multiplexer #(.select(2)) multiplexer_5 (
    .in0(_00_4), .in1(_01_4), .in2(_10_4), .in3(_11_4), .out(out_28), .sel(in_23));  // open: en

  // Notes on the sheet:
  //   NOT
  //   AND
  //   OR
  //   XOR
  //   XNOR
endmodule
