// Logisim project estudosomdosproutos.circ as structural Verilog: 1 circuit, main circuit main
module main (
  input  P,
  input  F,
  input  I,
  input  P_2,
  input  F_2,
  input  I_2,
  output out_7,
  output out_8
);

  wire and_1_out, and_2_out, and_3_out, and_4_out, and_5_out, and_6_out, and_7_out, not_1_out, not_2_out,
       not_3_out, not_4_out, not_5_out;

  not not_1 (not_1_out, P);
  not not_2 (not_2_out, F);
  not not_3 (not_3_out, I);
  and and_1 (and_1_out, not_1_out, not_2_out, not_3_out);
  and and_2 (and_2_out, not_1_out, not_2_out, I);
  and and_3 (and_3_out, not_1_out, F, not_3_out);
  and and_4 (and_4_out, not_1_out, F, I);
  and and_5 (and_5_out, P, F, not_3_out);
  not not_4 (not_4_out, P_2);
  not not_5 (not_5_out, I_2);
  or or_1 (out_7, and_1_out, and_2_out, and_3_out, and_4_out, and_5_out);
  and and_6 (and_6_out, not_5_out, F_2, P_2);
  buf and_7 (and_7_out, not_4_out);  // AND_Gate
  or or_2 (out_8, and_6_out, and_7_out);
endmodule
