// Logisim project experiencia05.circ as structural Verilog: 2 circuits, main circuit Contador 5 bits
module Contador_5_bits (
  input  Clock,
  input  Preset,
  input  Enable,
  input  Clear,
  output Q4,
  output Q3,
  output Q2,
  output Q1,
  output Q0
);

  wire not_1_out, not_2_out, not_3_out, not_4_out, not_5_out;

  not not_1 (not_1_out, Q0);
  D_Flip_Flop d_ff_1 (.clk(Clock), .D(not_1_out), .Q(Q0), .preset(Preset), .en(Enable), .reset(Clear));  // open: Qn
  D_Flip_Flop d_ff_2 (.clk(not_1_out), .D(not_2_out), .Q(Q1), .preset(Preset), .en(Enable), .reset(Clear));  // open: Qn
  not not_2 (not_2_out, Q1);
  D_Flip_Flop d_ff_3 (.clk(not_2_out), .D(not_3_out), .Q(Q2), .preset(Preset), .en(Enable), .reset(Clear));  // open: Qn
  D_Flip_Flop d_ff_4 (.clk(not_3_out), .D(not_4_out), .Q(Q3), .preset(Preset), .en(Enable), .reset(Clear));  // open: Qn
  not not_3 (not_3_out, Q2);
  not not_4 (not_4_out, Q3);
  D_Flip_Flop d_ff_5 (.clk(not_4_out), .D(not_5_out), .Q(Q4), .preset(Preset), .en(Enable), .reset(Clear));  // open: Qn
  not not_5 (not_5_out, Q4);
endmodule

module Tarefa (
  input  Clear,
  input  Enale,
  input  Preset,
  input  in_4,
  input  in_5
);

  wire Clock_out, contador_5_bits_1_q0, contador_5_bits_1_q1, contador_5_bits_1_q2, contador_5_bits_1_q3,
       contador_5_bits_1_q4, tarefa01_1_a, tarefa01_1_a0, tarefa01_1_b, tarefa01_1_b0, tarefa01_1_c,
       tarefa01_1_c0, tarefa01_1_d, tarefa01_1_d0, tarefa01_1_e, tarefa01_1_e0, tarefa01_1_f, tarefa01_1_f0,
       tarefa01_1_g, tarefa01_1_g0;

  Contador_5_bits contador_5_bits_1 (
    .Clock(Clock_out), .Preset(Preset), .Enable(Enale), .Clear(Clear), .Q4(contador_5_bits_1_q4),
    .Q3(contador_5_bits_1_q3), .Q2(contador_5_bits_1_q2), .Q1(contador_5_bits_1_q1), .Q0(contador_5_bits_1_q0));
  Clock Clock (.out(Clock_out));
  tarefa01 tarefa01_1 (
    .S4(contador_5_bits_1_q4), .S3(contador_5_bits_1_q3), .S2(contador_5_bits_1_q2),
    .S1(contador_5_bits_1_q1), .S0(contador_5_bits_1_q0), .in_6(in_4), .in_7(in_5), .b(tarefa01_1_b),
    .a(tarefa01_1_a), .f(tarefa01_1_f), .g(tarefa01_1_g), .e(tarefa01_1_e), .d(tarefa01_1_d),
    .c(tarefa01_1_c), .b0(tarefa01_1_b0), .a0(tarefa01_1_a0), .f0(tarefa01_1_f0), .g0(tarefa01_1_g0),
    .e0(tarefa01_1_e0), .d0(tarefa01_1_d0), .c0(tarefa01_1_c0));
  _7_Segment_Display u_7_segment_display_1 (
    .g(tarefa01_1_g), .f(tarefa01_1_f), .a(tarefa01_1_a), .b(tarefa01_1_b), .e(tarefa01_1_e),
    .d(tarefa01_1_d), .c(tarefa01_1_c));  // open: dp
  _7_Segment_Display u_7_segment_display_2 (
    .g(tarefa01_1_g0), .f(tarefa01_1_f0), .a(tarefa01_1_a0), .b(tarefa01_1_b0), .e(tarefa01_1_e0),
    .d(tarefa01_1_d0), .c(tarefa01_1_c0));  // open: dp

  // Notes on the sheet:
  //   Dezena
  //   Unidade
endmodule
