// Logisim project experiência03.circ as structural Verilog: 4 circuits, main circuit Somador
module Somador (
  input  A,
  input  B,
  input  Cin,
  output S,
  output Cout
);

  wire and_1_out, and_2_out, xor_1_out;

  xor xor_1 (xor_1_out, A, B);
  xor xor_2 (S, xor_1_out, Cin);
  and and_1 (and_1_out, Cin, xor_1_out);
  and and_2 (and_2_out, A, B);
  xor xor_3 (Cout, and_1_out, and_2_out);

  // Notes on the sheet:
  //   Somador Completo
endmodule

module Somador_4_bits (
  input  Cin,
  input  A0,
  input  B0,
  input  A1,
  input  B1,
  input  A2,
  input  B2,
  input  A3,
  input  B3,
  output S0,
  output S1,
  output S2,
  output S3,
  output Cout
);

  wire somador_1_cout, somador_2_cout, somador_3_cout;

  Somador somador_1 (.A(A0), .B(B0), .Cin(Cin), .S(S0), .Cout(somador_1_cout));
  Somador somador_2 (.A(A1), .B(B1), .Cin(somador_1_cout), .S(S1), .Cout(somador_2_cout));
  Somador somador_3 (.A(A2), .B(B2), .Cin(somador_2_cout), .S(S2), .Cout(somador_3_cout));
  Somador somador_4 (.A(A3), .B(B3), .Cin(somador_3_cout), .S(S3), .Cout(Cout));

  // Notes on the sheet:
  //   Somador de 4 bits
endmodule

module Complemento_de_dois (
  input  C1,
  input  A3,
  input  A2,
  input  A1,
  input  A0,
  input  Adicionar_0001,
  input  in_7,
  input  in_8,
  input  in_9,
  input  Cin,
  output Cout,
  output S3,
  output S2,
  output S1,
  output S0
);

  wire controlled_inverter_1_out, controlled_inverter_2_out, controlled_inverter_3_out,
       controlled_inverter_4_out;

  assign controlled_inverter_1_out = C1 ? ~A3 : 1'bz;  // Controlled_Inverter controlled_inverter_1
  assign controlled_inverter_2_out = C1 ? ~A1 : 1'bz;  // Controlled_Inverter controlled_inverter_2
  assign controlled_inverter_3_out = C1 ? ~A2 : 1'bz;  // Controlled_Inverter controlled_inverter_3
  Somador_4_bits somador_4_bits_1 (
    .A0(controlled_inverter_4_out), .B0(in_9), .A1(controlled_inverter_2_out), .B1(in_8),
    .A2(controlled_inverter_3_out), .B2(in_7), .A3(controlled_inverter_1_out), .B3(Adicionar_0001),
    .Cin(Cin), .S0(S0), .S1(S1), .S2(S2), .S3(S3), .Cout(Cout));
  assign controlled_inverter_4_out = C1 ? ~A0 : 1'bz;  // Controlled_Inverter controlled_inverter_4

  // Notes on the sheet:
  //   Complemento de 2
  //   Complemento de 1
  //   Entradas
endmodule

module Subtrator (
  input  in_1,
  input  B3,
  input  B2,
  input  B1,
  input  B0,
  input  A3,
  input  A2,
  input  A1,
  input  A0,
  input  in_10,
  input  in_11,
  input  in_12,
  input  in_13,
  input  Cin,
  output out_15,
  output S3,
  output S2,
  output S1,
  output S0
);

  wire complemento_de_dois_1_cout, complemento_de_dois_1_s0, complemento_de_dois_1_s1,
       complemento_de_dois_1_s2, complemento_de_dois_1_s3, somador_4_bits_1_cout;

  Complemento_de_dois complemento_de_dois_1 (
    .Adicionar_0001(in_10), .in_7(in_11), .in_8(in_12), .in_9(in_13), .C1(in_1), .A3(B3), .A2(B2), .A1(B1),
    .A0(B0), .Cout(complemento_de_dois_1_cout), .S3(complemento_de_dois_1_s3), .S2(complemento_de_dois_1_s2),
    .S1(complemento_de_dois_1_s1), .S0(complemento_de_dois_1_s0), .Cin(Cin));
  Somador_4_bits somador_4_bits_1 (
    .A0(A0), .B0(complemento_de_dois_1_s0), .A1(A1), .B1(complemento_de_dois_1_s1), .A2(A2),
    .B2(complemento_de_dois_1_s2), .A3(A3), .B3(complemento_de_dois_1_s3), .Cin(complemento_de_dois_1_cout),
    .S0(S0), .S1(S1), .S2(S2), .S3(S3), .Cout(somador_4_bits_1_cout));
  not not_1 (out_15, somador_4_bits_1_cout);

  // Notes on the sheet:
  //   Complemento de 1
  //   Adicionar0001
  //   Entradas B
  //   Complemento de 2
  //   Subtrator
  //   Somador
  //   Bits do Resultado
  //   Entradas A
endmodule
