// Logisim project experiência03Complemento.circ as structural Verilog: 1 circuit, main circuit main
module main (
  input  in_1,
  input  in_2,
  input  in_3,
  input  in_4,
  input  in_5,
  input  in_6,
  input  in_7,
  output out_8,
  output out_9,
  output out_10,
  output out_11,
  output out_12
);

  wire adder_1_cout, adder_1_out, adder_2_cout, adder_2_out, adder_3_cout, adder_3_out, adder_4_out;

  Adder #(.width(1)) adder_1 (.a(in_4), .b(in_1), .out(adder_1_out), .cin(in_3), .cout(adder_1_cout));
  Adder #(.width(1)) adder_2 (.a(in_5), .b(in_1), .out(adder_2_out), .cin(adder_1_cout), .cout(adder_2_cout));
  Adder #(.width(1)) adder_3 (.a(in_6), .b(in_1), .out(adder_3_out), .cin(adder_2_cout), .cout(adder_3_cout));
  Adder #(.width(1)) adder_4 (.a(in_7), .b(in_1), .out(adder_4_out), .cin(adder_3_cout), .cout(out_12));
  assign out_8 = in_2 ? ~adder_1_out : 1'bz;  // Controlled_Inverter controlled_inverter_1
  assign out_9 = in_2 ? ~adder_2_out : 1'bz;  // Controlled_Inverter controlled_inverter_2
  assign out_10 = in_2 ? ~adder_3_out : 1'bz;  // Controlled_Inverter controlled_inverter_3
  assign out_11 = in_2 ? ~adder_4_out : 1'bz;  // Controlled_Inverter controlled_inverter_4

  // Notes on the sheet:
  //   Complemento de dois com Somador e inversor
endmodule
