// Logisim project experiência03Subtrator.circ as structural Verilog: 1 circuit, main circuit main
module main (
  input  in_1,
  input  in_2,
  input  A0,
  input  B0,
  input  A1,
  input  B1,
  input  A2,
  input  B2,
  input  A3,
  input  B3,
  input  in_11,
  input  in_12,
  input  A0_2,
  input  in_14,
  input  A1_2,
  input  in_16,
  input  A2_2,
  input  in_18,
  input  A3_2,
  input  in_20,
  output out_21,
  output out_22,
  output out_23,
  output out_24,
  output out_25,
  output out_26,
  output out_27,
  output out_28,
  output out_29,
  output out_30
);

  wire adder_1_cout, adder_2_cout, adder_3_cout, adder_5_cout, adder_5_out, adder_6_cout, adder_6_out,
       adder_7_cout, adder_7_out, adder_8_out, adder_9_cout, adder_10_cout, adder_11_cout,
       controlled_inverter_1_out, controlled_inverter_2_out, controlled_inverter_3_out,
       controlled_inverter_4_out, controlled_inverter_5_out, controlled_inverter_6_out,
       controlled_inverter_7_out, controlled_inverter_8_out;

  assign controlled_inverter_1_out = in_2 ? ~B0 : 1'bz;  // Controlled_Inverter controlled_inverter_1
  assign controlled_inverter_2_out = in_2 ? ~B1 : 1'bz;  // Controlled_Inverter controlled_inverter_2
  assign controlled_inverter_3_out = in_2 ? ~B2 : 1'bz;  // Controlled_Inverter controlled_inverter_3
  assign controlled_inverter_4_out = in_2 ? ~B3 : 1'bz;  // Controlled_Inverter controlled_inverter_4
  Adder #(.width(1)) adder_1 (.a(A0), .b(controlled_inverter_1_out), .out(out_21), .cin(in_1), .cout(adder_1_cout));
  Adder #(.width(1)) adder_2 (
    .a(A1), .b(controlled_inverter_2_out), .out(out_22), .cin(adder_1_cout), .cout(adder_2_cout));
  Adder #(.width(1)) adder_3 (
    .a(A2), .b(controlled_inverter_3_out), .out(out_23), .cin(adder_2_cout), .cout(adder_3_cout));
  Adder #(.width(1)) adder_4 (.a(A3), .b(controlled_inverter_4_out), .out(out_24), .cin(adder_3_cout), .cout(out_25));
  Adder #(.width(1)) adder_5 (.a(in_14), .b(in_11), .out(adder_5_out), .cout(adder_5_cout));  // open: cin
  Adder #(.width(1)) adder_6 (.a(in_16), .b(in_11), .out(adder_6_out), .cin(adder_5_cout), .cout(adder_6_cout));
  Adder #(.width(1)) adder_7 (.a(in_18), .b(in_11), .out(adder_7_out), .cin(adder_6_cout), .cout(adder_7_cout));
  Adder #(.width(1)) adder_8 (.a(in_20), .b(in_11), .out(adder_8_out), .cin(adder_7_cout));  // open: cout
  assign controlled_inverter_5_out = in_12 ? ~adder_5_out : 1'bz;  // Controlled_Inverter controlled_inverter_5
  assign controlled_inverter_6_out = in_12 ? ~adder_6_out : 1'bz;  // Controlled_Inverter controlled_inverter_6
  assign controlled_inverter_7_out = in_12 ? ~adder_7_out : 1'bz;  // Controlled_Inverter controlled_inverter_7
  assign controlled_inverter_8_out = in_12 ? ~adder_8_out : 1'bz;  // Controlled_Inverter controlled_inverter_8
  Adder #(.width(1)) adder_9 (.a(A0_2), .b(controlled_inverter_5_out), .out(out_26), .cout(adder_9_cout));  // open: cin
  Adder #(.width(1)) adder_10 (
    .a(A1_2), .b(controlled_inverter_6_out), .out(out_27), .cin(adder_9_cout), .cout(adder_10_cout));
  Adder #(.width(1)) adder_11 (
    .a(A2_2), .b(controlled_inverter_7_out), .out(out_28), .cin(adder_10_cout), .cout(adder_11_cout));
  Adder #(.width(1)) adder_12 (
    .a(A3_2), .b(controlled_inverter_8_out), .out(out_29), .cin(adder_11_cout), .cout(out_30));
endmodule
