// Logisim project experiência6.circ as structural Verilog: 6 circuits, main circuit Contador de 6 bits
module Contador_de_6_bits (
  input  Clock,
  input  Preset,
  input  Enable,
  input  Clear,
  output Q5,
  output Q4,
  output Q3,
  output Q2,
  output Q1,
  output Q0
);

  wire not_1_out, not_2_out, not_3_out, not_4_out, not_5_out, not_6_out;

  D_Flip_Flop d_ff_1 (.clk(Clock), .D(not_1_out), .Q(Q0), .preset(Preset), .en(Enable), .reset(Clear));  // open: Qn
  not not_1 (not_1_out, Q0);
  D_Flip_Flop d_ff_2 (.clk(not_1_out), .D(not_2_out), .Q(Q1), .preset(Preset), .en(Enable), .reset(Clear));  // open: Qn
  not not_2 (not_2_out, Q1);
  D_Flip_Flop d_ff_3 (.clk(not_2_out), .D(not_3_out), .Q(Q2), .preset(Preset), .en(Enable), .reset(Clear));  // open: Qn
  D_Flip_Flop d_ff_4 (.clk(not_3_out), .D(not_4_out), .Q(Q3), .preset(Preset), .en(Enable), .reset(Clear));  // open: Qn
  not not_3 (not_3_out, Q2);
  not not_4 (not_4_out, Q3);
  D_Flip_Flop d_ff_5 (.clk(not_4_out), .D(not_5_out), .Q(Q4), .preset(Preset), .en(Enable), .reset(Clear));  // open: Qn
  D_Flip_Flop d_ff_6 (.clk(not_5_out), .D(not_6_out), .Q(Q5), .preset(Preset), .en(Enable), .reset(Clear));  // open: Qn
  not not_5 (not_5_out, Q4);
  not not_6 (not_6_out, Q5);

  // Notes on the sheet:
  //   Contador 6 Bits
endmodule

module contador6bitsDecimal (
  input  Clear,
  input  Enable,
  input  Preset,
  input  in_4
);

  wire Clock_out, contador_de_6_bits_1_q0, contador_de_6_bits_1_q1, contador_de_6_bits_1_q2,
       contador_de_6_bits_1_q3, contador_de_6_bits_1_q4, contador_de_6_bits_1_q5, tarefa01_1_a,
       tarefa01_1_a0, tarefa01_1_b, tarefa01_1_b0, tarefa01_1_c, tarefa01_1_c0, tarefa01_1_d, tarefa01_1_d0,
       tarefa01_1_e, tarefa01_1_e0, tarefa01_1_f, tarefa01_1_f0, tarefa01_1_g, tarefa01_1_g0;

  Contador_de_6_bits contador_de_6_bits_1 (
    .Clock(Clock_out), .Preset(Preset), .Enable(Enable), .Clear(Clear), .Q5(contador_de_6_bits_1_q5),
    .Q4(contador_de_6_bits_1_q4), .Q3(contador_de_6_bits_1_q3), .Q2(contador_de_6_bits_1_q2),
    .Q1(contador_de_6_bits_1_q1), .Q0(contador_de_6_bits_1_q0));
  Clock Clock (.out(Clock_out));
  tarefa01 tarefa01_1 (
    .S4(contador_de_6_bits_1_q4), .S3(contador_de_6_bits_1_q3), .S2(contador_de_6_bits_1_q2),
    .S1(contador_de_6_bits_1_q1), .S0(contador_de_6_bits_1_q0), .in_6(contador_de_6_bits_1_q5), .in_7(in_4),
    .b(tarefa01_1_b), .a(tarefa01_1_a), .f(tarefa01_1_f), .g(tarefa01_1_g), .e(tarefa01_1_e),
    .d(tarefa01_1_d), .c(tarefa01_1_c), .b0(tarefa01_1_b0), .a0(tarefa01_1_a0), .f0(tarefa01_1_f0),
    .g0(tarefa01_1_g0), .e0(tarefa01_1_e0), .d0(tarefa01_1_d0), .c0(tarefa01_1_c0));
  _7_Segment_Display u_7_segment_display_1 (
    .g(tarefa01_1_g), .f(tarefa01_1_f), .a(tarefa01_1_a), .b(tarefa01_1_b), .e(tarefa01_1_e),
    .d(tarefa01_1_d), .c(tarefa01_1_c));  // open: dp
  _7_Segment_Display u_7_segment_display_2 (
    .g(tarefa01_1_g0), .f(tarefa01_1_f0), .a(tarefa01_1_a0), .b(tarefa01_1_b0), .e(tarefa01_1_e0),
    .d(tarefa01_1_d0), .c(tarefa01_1_c0));  // open: dp

  // Notes on the sheet:
  //   Unidade
  //   Dezena
endmodule

module paralelo_paralelo (
  input  D0,
  input  D1,
  input  D2,
  input  D3,
  input  Clock,
  output Q0,
  output Q1,
  output Q2,
  output Q3
);

  D_Flip_Flop d_ff_1 (.clk(Clock), .D(D0), .Q(Q0));  // open: Qn, preset, en, reset
  D_Flip_Flop d_ff_2 (.clk(Clock), .D(D1), .Q(Q1));  // open: Qn, preset, en, reset
  D_Flip_Flop d_ff_3 (.clk(Clock), .D(D2), .Q(Q2));  // open: Qn, preset, en, reset
  D_Flip_Flop d_ff_4 (.clk(Clock), .D(D3), .Q(Q3));  // open: Qn, preset, en, reset

  // Notes on the sheet:
  //   Registrador Paralelo-Paralelo
endmodule

module serie_paralelo (
  input  D0,
  input  Clock,
  output Q0,
  output Q1,
  output Q2,
  output Q3
);

  D_Flip_Flop d_ff_1 (.clk(Clock), .D(D0), .Q(Q0));  // open: Qn, preset, en, reset
  D_Flip_Flop d_ff_2 (.clk(Clock), .D(Q0), .Q(Q1));  // open: Qn, preset, en, reset
  D_Flip_Flop d_ff_3 (.clk(Clock), .D(Q1), .Q(Q2));  // open: Qn, preset, en, reset
  D_Flip_Flop d_ff_4 (.clk(Clock), .D(Q2), .Q(Q3));  // open: Qn, preset, en, reset
endmodule

module Somapp (
  input  Cin,
  input  A0,
  input  A1,
  input  A2,
  input  A3,
  input  B0,
  input  B1,
  input  B2,
  input  in_9,
  input  B3,
  input  in_11
);

  wire ClockA_out, ClockB_out, paralelo_paralelo_1_q0, paralelo_paralelo_1_q1, paralelo_paralelo_1_q2,
       paralelo_paralelo_1_q3, paralelo_paralelo_2_q0, paralelo_paralelo_2_q1, paralelo_paralelo_2_q2,
       paralelo_paralelo_2_q3, somador_4_bits_1_cout, somador_4_bits_1_s0, somador_4_bits_1_s1,
       somador_4_bits_1_s2, somador_4_bits_1_s3, tarefa01_1_a, tarefa01_1_a0, tarefa01_1_b, tarefa01_1_b0,
       tarefa01_1_c, tarefa01_1_c0, tarefa01_1_d, tarefa01_1_d0, tarefa01_1_e, tarefa01_1_e0, tarefa01_1_f,
       tarefa01_1_f0, tarefa01_1_g, tarefa01_1_g0;

  Clock ClockB (.out(ClockB_out));
  Clock ClockA (.out(ClockA_out));
  paralelo_paralelo paralelo_paralelo_1 (
    .D0(A0), .D1(A1), .D2(A2), .D3(A3), .Clock(ClockA_out), .Q0(paralelo_paralelo_1_q0),
    .Q1(paralelo_paralelo_1_q1), .Q2(paralelo_paralelo_1_q2), .Q3(paralelo_paralelo_1_q3));
  paralelo_paralelo paralelo_paralelo_2 (
    .D0(B0), .D1(B1), .D2(B2), .D3(B3), .Clock(ClockB_out), .Q0(paralelo_paralelo_2_q0),
    .Q1(paralelo_paralelo_2_q1), .Q2(paralelo_paralelo_2_q2), .Q3(paralelo_paralelo_2_q3));
  Somador_4_bits somador_4_bits_1 (
    .A0(paralelo_paralelo_1_q0), .B0(paralelo_paralelo_2_q0), .A1(paralelo_paralelo_1_q1),
    .B1(paralelo_paralelo_2_q1), .A2(paralelo_paralelo_1_q2), .B2(paralelo_paralelo_2_q2),
    .A3(paralelo_paralelo_1_q3), .B3(paralelo_paralelo_2_q3), .Cin(Cin), .S0(somador_4_bits_1_s0),
    .S1(somador_4_bits_1_s1), .S2(somador_4_bits_1_s2), .S3(somador_4_bits_1_s3), .Cout(somador_4_bits_1_cout));
  tarefa01 tarefa01_1 (
    .S4(somador_4_bits_1_cout), .S3(somador_4_bits_1_s3), .S2(somador_4_bits_1_s2), .S1(somador_4_bits_1_s1),
    .S0(somador_4_bits_1_s0), .in_6(in_9), .in_7(in_11), .b(tarefa01_1_b), .a(tarefa01_1_a),
    .f(tarefa01_1_f), .g(tarefa01_1_g), .e(tarefa01_1_e), .d(tarefa01_1_d), .c(tarefa01_1_c),
    .b0(tarefa01_1_b0), .a0(tarefa01_1_a0), .f0(tarefa01_1_f0), .g0(tarefa01_1_g0), .e0(tarefa01_1_e0),
    .d0(tarefa01_1_d0), .c0(tarefa01_1_c0));
  _7_Segment_Display u_7_segment_display_1 (
    .g(tarefa01_1_g), .f(tarefa01_1_f), .a(tarefa01_1_a), .b(tarefa01_1_b), .e(tarefa01_1_e),
    .d(tarefa01_1_d), .c(tarefa01_1_c));  // open: dp
  _7_Segment_Display u_7_segment_display_2 (
    .g(tarefa01_1_g0), .f(tarefa01_1_f0), .a(tarefa01_1_a0), .b(tarefa01_1_b0), .e(tarefa01_1_e0),
    .d(tarefa01_1_d0), .c(tarefa01_1_c0));  // open: dp

  // Notes on the sheet:
  //   Unidade
  //   Dezena
endmodule

module Somasp (
  input  Cin,
  input  A0,
  input  B0,
  input  in_4,
  input  in_5
);

  wire clock_1_out, clock_2_out, serie_paralelo_1_q0, serie_paralelo_1_q1, serie_paralelo_1_q2,
       serie_paralelo_1_q3, serie_paralelo_2_q0, serie_paralelo_2_q1, serie_paralelo_2_q2,
       serie_paralelo_2_q3, somador_4_bits_1_cout, somador_4_bits_1_s0, somador_4_bits_1_s1,
       somador_4_bits_1_s2, somador_4_bits_1_s3, tarefa01_1_a, tarefa01_1_a0, tarefa01_1_b, tarefa01_1_b0,
       tarefa01_1_c, tarefa01_1_c0, tarefa01_1_d, tarefa01_1_d0, tarefa01_1_e, tarefa01_1_e0, tarefa01_1_f,
       tarefa01_1_f0, tarefa01_1_g, tarefa01_1_g0;

  Clock clock_1 (.out(clock_1_out));
  Clock clock_2 (.out(clock_2_out));
  serie_paralelo serie_paralelo_1 (
    .D0(A0), .Clock(clock_1_out), .Q0(serie_paralelo_1_q0), .Q1(serie_paralelo_1_q1),
    .Q2(serie_paralelo_1_q2), .Q3(serie_paralelo_1_q3));
  serie_paralelo serie_paralelo_2 (
    .D0(B0), .Clock(clock_2_out), .Q0(serie_paralelo_2_q0), .Q1(serie_paralelo_2_q1),
    .Q2(serie_paralelo_2_q2), .Q3(serie_paralelo_2_q3));
  Somador_4_bits somador_4_bits_1 (
    .A0(serie_paralelo_1_q0), .B0(serie_paralelo_2_q0), .A1(serie_paralelo_1_q1), .B1(serie_paralelo_2_q1),
    .A2(serie_paralelo_1_q2), .B2(serie_paralelo_2_q2), .A3(serie_paralelo_1_q3), .B3(serie_paralelo_2_q3),
    .Cin(Cin), .S0(somador_4_bits_1_s0), .S1(somador_4_bits_1_s1), .S2(somador_4_bits_1_s2),
    .S3(somador_4_bits_1_s3), .Cout(somador_4_bits_1_cout));
  tarefa01 tarefa01_1 (
    .S4(somador_4_bits_1_cout), .S3(somador_4_bits_1_s3), .S2(somador_4_bits_1_s2), .S1(somador_4_bits_1_s1),
    .S0(somador_4_bits_1_s0), .in_6(in_4), .in_7(in_5), .b(tarefa01_1_b), .a(tarefa01_1_a), .f(tarefa01_1_f),
    .g(tarefa01_1_g), .e(tarefa01_1_e), .d(tarefa01_1_d), .c(tarefa01_1_c), .b0(tarefa01_1_b0),
    .a0(tarefa01_1_a0), .f0(tarefa01_1_f0), .g0(tarefa01_1_g0), .e0(tarefa01_1_e0), .d0(tarefa01_1_d0),
    .c0(tarefa01_1_c0));
  _7_Segment_Display u_7_segment_display_1 (
    .g(tarefa01_1_g), .f(tarefa01_1_f), .a(tarefa01_1_a), .b(tarefa01_1_b), .e(tarefa01_1_e),
    .d(tarefa01_1_d), .c(tarefa01_1_c));  // open: dp
  _7_Segment_Display u_7_segment_display_2 (
    .g(tarefa01_1_g0), .f(tarefa01_1_f0), .a(tarefa01_1_a0), .b(tarefa01_1_b0), .e(tarefa01_1_e0),
    .d(tarefa01_1_d0), .c(tarefa01_1_c0));  // open: dp

  // Notes on the sheet:
  //   Unidade
  //   Dezena
endmodule
