// Logisim project led de 7 segmentos trabalho 2.circ as structural Verilog: 1 circuit, main circuit main
// b
module main (
  input  in_1,
  input  in_2,
  input  in_3,
  input  in_4,
  input  in_5,
  input  in_6,
  input  in_7,
  input  in_8,
  input  in_9,
  input  in_10,
  input  in_11,
  input  in_12,
  input  in_13,
  input  in_14,
  input  in_15,
  input  in_16,
  input  in_17,
  input  in_18,
  input  in_19,
  input  in_20,
  input  in_21,
  input  in_22,
  input  in_23,
  input  in_24,
  input  in_25,
  input  in_26,
  input  in_27,
  input  in_28,
  input  in_29,
  input  in_30,
  input  in_31,
  input  in_32,
  input  in_33,
  input  in_34,
  input  in_35,
  input  in_36,
  input  in_37,
  input  in_38,
  input  in_39,
  input  in_40,
  input  in_41,
  input  in_42,
  input  in_43,
  input  in_44,
  input  in_45,
  input  in_46,
  input  in_47,
  input  in_48,
  input  g,
  input  in_50,
  input  in_51,
  input  in_52,
  input  in_53,
  input  in_54,
  input  in_55,
  input  in_56,
  input  in_57,
  input  [3:0] ABCD,
  input  in_59,
  input  in_60,
  input  in_61,
  input  in_62,
  input  in_63,
  input  in_64,
  input  in_65,
  input  e,
  input  in_67,
  input  in_68,
  input  in_69,
  input  in_70,
  input  in_71,
  input  in_72,
  input  in_73,
  input  in_74,
  input  in_75,
  input  in_76,
  input  in_77,
  input  in_78,
  input  in_79,
  input  in_80,
  input  in_81,
  input  in_82,
  input  in_83,
  input  in_84,
  input  in_85,
  input  in_86,
  input  in_87,
  input  in_88,
  input  in_89,
  input  in_90,
  input  in_91,
  input  in_92,
  input  in_93,
  input  in_94,
  input  in_95,
  input  in_96,
  input  in_97,
  input  in_98,
  input  in_99,
  input  in_100,
  input  in_101,
  input  in_102,
  input  in_103,
  input  in_104,
  input  in_105,
  input  in_106,
  input  in_107,
  input  in_108,
  input  in_109,
  input  in_110,
  input  in_111,
  input  in_112,
  input  in_113,
  output f,
  output a,
  output g_2,
  output b,
  output e_2,
  output d,
  output c
);

  Multiplexer #(.select(4), .enable("false")) multiplexer_1 (
    .in0(in_3), .in1(in_6), .in2(in_9), .in3(in_12), .in4(in_15), .in5(in_18), .in6(in_21), .in7(in_24),
    .in8(in_27), .in9(in_30), .in10(in_33), .in11(in_36), .in12(in_39), .in13(in_42), .in14(in_45),
    .in15(in_48), .out(f), .sel(ABCD));
  Multiplexer #(.select(4), .enable("false")) multiplexer_2 (
    .in0(g), .in1(in_50), .in2(in_51), .in3(in_52), .in4(in_53), .in5(in_54), .in6(in_55), .in7(in_56),
    .in8(in_57), .in9(in_59), .in10(in_60), .in11(in_61), .in12(in_62), .in13(in_63), .in14(in_64),
    .in15(in_65), .out(g_2), .sel(ABCD));
  Multiplexer #(.select(4), .enable("false")) multiplexer_3 (
    .in0(e), .in1(in_67), .in2(in_68), .in3(in_69), .in4(in_70), .in5(in_71), .in6(in_72), .in7(in_73),
    .in8(in_74), .in9(in_75), .in10(in_76), .in11(in_79), .in12(in_82), .in13(in_85), .in14(in_88),
    .in15(in_91), .out(e_2), .sel(ABCD));
  Multiplexer #(.select(4), .enable("false")) multiplexer_4 (
    .in0(in_1), .in1(in_4), .in2(in_7), .in3(in_10), .in4(in_13), .in5(in_16), .in6(in_19), .in7(in_22),
    .in8(in_25), .in9(in_28), .in10(in_31), .in11(in_34), .in12(in_37), .in13(in_40), .in14(in_43),
    .in15(in_46), .out(a), .sel(ABCD));
  Multiplexer #(.select(4), .enable("false")) multiplexer_5 (
    .in0(in_78), .in1(in_81), .in2(in_84), .in3(in_87), .in4(in_90), .in5(in_93), .in6(in_95), .in7(in_97),
    .in8(in_99), .in9(in_101), .in10(in_103), .in11(in_105), .in12(in_107), .in13(in_109), .in14(in_111),
    .in15(in_113), .out(d), .sel(ABCD));
  _7_Segment_Display u_7_segment_display_1 (.g(g_2), .f(f), .a(a), .b(b), .e(e_2), .d(d), .c(c));  // open: dp
  Multiplexer #(.select(4), .enable("false")) multiplexer_6 (
    .in0(in_2), .in1(in_5), .in2(in_8), .in3(in_11), .in4(in_14), .in5(in_17), .in6(in_20), .in7(in_23),
    .in8(in_26), .in9(in_29), .in10(in_32), .in11(in_35), .in12(in_38), .in13(in_41), .in14(in_44),
    .in15(in_47), .out(b), .sel(ABCD));
  Multiplexer #(.select(4), .enable("false")) multiplexer_7 (
    .in0(in_77), .in1(in_80), .in2(in_83), .in3(in_86), .in4(in_89), .in5(in_92), .in6(in_94), .in7(in_96),
    .in8(in_98), .in9(in_100), .in10(in_102), .in11(in_104), .in12(in_106), .in13(in_108), .in14(in_110),
    .in15(in_112), .out(c), .sel(ABCD));

  // Notes on the sheet:
  //   f
  //   d
  //   a
  //   b
  //   c
endmodule
