// Logisim project processaor 183.circ as structural Verilog: 1 circuit, main circuit main
module main (
  input  VEM_UM,
  input  INVA,
  input  A,
  input  B,
  input  F0,
  input  F1,
  output SAIDA,
  output VAI_UM
);

  wire A_B_2_out, A_B_out, and_1_out, and_2_out, and_3_out, and_4_out, and_5_out, and_6_out, and_7_out,
       and_8_out, and_9_out, and_10_out, B_prime_out, not_1_out, not_2_out, not_3_out, not_4_out, xor_1_out,
       xor_2_out, xor_3_out;

  not not_1 (not_1_out, F0);
  not not_2 (not_2_out, F1);
  not not_3 (not_3_out, F0);
  not not_4 (not_4_out, F1);
  and and_1 (and_1_out, not_1_out, not_2_out);
  and and_2 (and_2_out, not_3_out, F1);
  and and_3 (and_3_out, F0, not_4_out);
  and and_4 (and_4_out, F0, F1);
  xor xor_1 (xor_1_out, INVA, A);
  and A_B (A_B_out, xor_1_out, B);
  or A_B_2 (A_B_2_out, xor_1_out, B);
  not B_prime (B_prime_out, B);
  and and_5 (and_5_out, and_1_out, A_B_out);
  and and_6 (and_6_out, and_2_out, A_B_2_out);
  and and_7 (and_7_out, and_3_out, B_prime_out);
  and and_8 (and_8_out, and_4_out, xor_1_out, B);
  xor xor_2 (xor_2_out, B, xor_1_out);
  or or_1 (VAI_UM, and_8_out, and_9_out);
  and and_9 (and_9_out, and_4_out, xor_2_out, VEM_UM);
  xor xor_3 (xor_3_out, VEM_UM, xor_2_out);
  and and_10 (and_10_out, xor_3_out, and_4_out);
  or or_2 (SAIDA, and_5_out, and_6_out, and_7_out, and_10_out);
endmodule
