// Logisim project somador completo de 3 números.circ as structural Verilog: 1 circuit, main circuit main
module main (
  input  VEM_UM,
  input  A,
  input  B,
  output SAIDA,
  output VAI_UM
);

  wire and_1_out, and_2_out, xor_1_out;

  and and_1 (and_1_out, B, A);
  xor xor_1 (xor_1_out, A, B);
  or or_1 (VAI_UM, and_1_out, and_2_out);
  and and_2 (and_2_out, xor_1_out, VEM_UM);
  xor xor_2 (SAIDA, VEM_UM, xor_1_out);

  // Notes on the sheet:
  //   Somador Completo
endmodule
