// Logisim project somador subtrator.circ as structural Verilog: 1 circuit, main circuit main
module main (
  input  B3,
  input  B2,
  input  B1,
  input  B0,
  input  A3,
  input  A2,
  input  A1,
  input  A0,
  input  Sub,
  output S1,
  output S3,
  output S0,
  output S2,
  output out_14
);

  wire and_1_out, and_2_out, and_3_out, and_4_out, and_5_out, and_6_out, and_7_out, and_8_out, or_1_out,
       or_2_out, or_3_out, or_4_out, xor_1_out, xor_2_out, xor_5_out, xor_6_out, xor_8_out, xor_9_out,
       xor_11_out, xor_12_out;

  xor xor_1 (xor_1_out, Sub, B3);
  and and_1 (and_1_out, xor_1_out, A3);
  xor xor_2 (xor_2_out, A3, xor_1_out);
  or or_1 (or_1_out, and_1_out, and_2_out);
  xor xor_3 (out_14, or_1_out, Sub);
  and and_2 (and_2_out, xor_2_out, or_2_out);
  xor xor_4 (S3, or_2_out, xor_2_out);
  xor xor_5 (xor_5_out, Sub, B2);
  and and_3 (and_3_out, xor_5_out, A2);
  xor xor_6 (xor_6_out, A2, xor_5_out);
  or or_2 (or_2_out, and_3_out, and_4_out);
  and and_4 (and_4_out, xor_6_out, or_3_out);
  xor xor_7 (S2, or_3_out, xor_6_out);
  xor xor_8 (xor_8_out, Sub, B1);
  and and_5 (and_5_out, xor_8_out, A1);
  xor xor_9 (xor_9_out, A1, xor_8_out);
  or or_3 (or_3_out, and_5_out, and_6_out);
  and and_6 (and_6_out, xor_9_out, or_4_out);
  xor xor_10 (S1, or_4_out, xor_9_out);
  xor xor_11 (xor_11_out, Sub, B0);
  and and_7 (and_7_out, xor_11_out, A0);
  xor xor_12 (xor_12_out, A0, xor_11_out);
  or or_4 (or_4_out, and_7_out, and_8_out);
  and and_8 (and_8_out, xor_12_out, Sub);
  xor xor_13 (S0, Sub, xor_12_out);
endmodule
