// Logisim project tarefa01e02 - Copia.circ as structural Verilog: 4 circuits, main circuit 74185
module _74185 (
  input  S4,
  input  S3,
  input  S2,
  input  S1,
  input  S0,
  output Y5,
  output Y4,
  output Y3,
  output Y2,
  output Y1,
  output Y0
);

  wire and_1_out, and_2_out, and_3_out, and_4_out, and_5_out, and_6_out, and_7_out, and_8_out, and_9_out,
       and_10_out, and_11_out, and_12_out, and_13_out, and_14_out, and_15_out, and_16_out, and_17_out,
       and_18_out, not_1_out, not_2_out, not_3_out, not_4_out, not_5_out, not_6_out, not_7_out, not_8_out,
       not_9_out, not_10_out, not_11_out, not_12_out, not_13_out, not_14_out, not_15_out, not_16_out,
       not_17_out, not_18_out, not_19_out, not_20_out, not_21_out, not_22_out, not_23_out, not_24_out,
       not_25_out;

  and and_1 (and_1_out, S4, S2);
  and and_2 (and_2_out, S4, S3);
  not not_1 (not_1_out, S4);
  not not_2 (not_2_out, S4);
  not not_3 (not_3_out, S3);
  not not_4 (not_4_out, S2);
  not not_5 (not_5_out, S4);
  not not_6 (not_6_out, S2);
  not not_7 (not_7_out, S1);
  not not_8 (not_8_out, S3);
  not not_9 (not_9_out, S2);
  not not_10 (not_10_out, S1);
  not not_11 (not_11_out, S4);
  not not_12 (not_12_out, S3);
  not not_13 (not_13_out, S4);
  not not_14 (not_14_out, S2);
  not not_15 (not_15_out, S1);
  not not_16 (not_16_out, S2);
  not not_17 (not_17_out, S4);
  not not_18 (not_18_out, S3);
  not not_19 (not_19_out, S3);
  not not_20 (not_20_out, S4);
  not not_21 (not_21_out, S1);
  not not_22 (not_22_out, S3);
  not not_23 (not_23_out, S2);
  not not_24 (not_24_out, S1);
  not not_25 (not_25_out, S2);
  or or_1 (Y5, and_1_out, and_2_out);
  and and_3 (and_3_out, not_1_out, S3, S1);
  and and_4 (and_4_out, not_2_out, S3, S2);
  and and_5 (and_5_out, S3, S2, S1);
  and and_6 (and_6_out, S4, not_3_out, not_4_out);
  and and_7 (and_7_out, not_5_out, S3, not_6_out, not_7_out);
  and and_8 (and_8_out, S4, not_8_out, not_9_out, S1);
  and and_9 (and_9_out, S4, S3, S2, not_10_out);
  and and_10 (and_10_out, not_11_out, not_12_out, S2);
  and and_11 (and_11_out, not_13_out, S2, S1);
  and and_12 (and_12_out, S4, not_14_out, not_15_out);
  and and_13 (and_13_out, S4, S3, not_16_out);
  and and_14 (and_14_out, not_17_out, not_18_out, S1);
  and and_15 (and_15_out, not_19_out, S2, S1);
  and and_16 (and_16_out, not_20_out, S3, S2, not_21_out);
  and and_17 (and_17_out, S4, not_22_out, not_23_out, not_24_out);
  and and_18 (and_18_out, S4, S3, not_25_out, S1);
  or or_2 (Y4, and_3_out, and_4_out, and_5_out, and_6_out);
  or or_3 (Y3, and_7_out, and_8_out, and_9_out);
  or or_4 (Y2, and_10_out, and_11_out, and_12_out, and_13_out);
  or or_5 (Y1, and_14_out, and_15_out, and_16_out, and_17_out, and_18_out);

  assign Y0 = S0;
endmodule

module tarefa01 (
  input  S4,
  input  S3,
  input  S2,
  input  S1,
  input  S0,
  input  in_6,
  input  in_7,
  output b,
  output a,
  output f,
  output g,
  output e,
  output d,
  output c,
  output b0,
  output a0,
  output f0,
  output g0,
  output e0,
  output d0,
  output c0
);

  wire n74185_1_y0, n74185_1_y1, n74185_1_y2, n74185_1_y3, n74185_1_y4, n74185_1_y5;

  _74185 u_74185_1 (
    .S4(S4), .S3(S3), .S2(S2), .S1(S1), .S0(S0), .Y5(n74185_1_y5), .Y4(n74185_1_y4), .Y3(n74185_1_y3),
    .Y2(n74185_1_y2), .Y1(n74185_1_y1), .Y0(n74185_1_y0));
  led_de_7_digitos_main main_1 (
    .A(n74185_1_y3), .B(n74185_1_y2), .C(n74185_1_y1), .D(n74185_1_y0), .b_2(b), .a_2(a), .f(f), .g(g),
    .e(e), .d_2(d), .c_2(c));
  led_de_7_digitos_main main_2 (
    .A(in_6), .B(in_7), .C(n74185_1_y5), .D(n74185_1_y4), .b_2(b0), .a_2(a0), .f(f0), .g(g0), .e(e0),
    .d_2(d0), .c_2(c0));
  _7_Segment_Display u_7_segment_display_1 (.g(g), .f(f), .a(a), .b(b), .e(e), .d(d), .c(c));  // open: dp
  _7_Segment_Display u_7_segment_display_2 (.g(g0), .f(f0), .a(a0), .b(b0), .e(e0), .d(d0), .c(c0));  // open: dp

  // Notes on the sheet:
  //   Entradas
  //   Display(Unidade)
  //   Display(Dezena)
endmodule

module tarefa02 (
  input  Cin,
  input  A0,
  input  A1,
  input  A2,
  input  A3,
  input  B0,
  input  B1,
  input  B2,
  input  B3,
  input  in_10,
  input  in_11
);

  wire somador_4_bits_1_cout, somador_4_bits_1_s0, somador_4_bits_1_s1, somador_4_bits_1_s2,
       somador_4_bits_1_s3, tarefa01_1_a, tarefa01_1_a0, tarefa01_1_b, tarefa01_1_b0, tarefa01_1_c,
       tarefa01_1_c0, tarefa01_1_d, tarefa01_1_d0, tarefa01_1_e, tarefa01_1_e0, tarefa01_1_f, tarefa01_1_f0,
       tarefa01_1_g, tarefa01_1_g0;

  Somador_4_bits somador_4_bits_1 (
    .A0(A0), .B0(B0), .A1(A1), .B1(B1), .A2(A2), .B2(B2), .A3(A3), .B3(B3), .Cin(Cin),
    .S0(somador_4_bits_1_s0), .S1(somador_4_bits_1_s1), .S2(somador_4_bits_1_s2), .S3(somador_4_bits_1_s3),
    .Cout(somador_4_bits_1_cout));
  tarefa01 tarefa01_1 (
    .S4(somador_4_bits_1_cout), .S3(somador_4_bits_1_s3), .S2(somador_4_bits_1_s2), .S1(somador_4_bits_1_s1),
    .S0(somador_4_bits_1_s0), .in_6(in_10), .in_7(in_11), .b(tarefa01_1_b), .a(tarefa01_1_a),
    .f(tarefa01_1_f), .g(tarefa01_1_g), .e(tarefa01_1_e), .d(tarefa01_1_d), .c(tarefa01_1_c),
    .b0(tarefa01_1_b0), .a0(tarefa01_1_a0), .f0(tarefa01_1_f0), .g0(tarefa01_1_g0), .e0(tarefa01_1_e0),
    .d0(tarefa01_1_d0), .c0(tarefa01_1_c0));
  _7_Segment_Display u_7_segment_display_1 (
    .g(tarefa01_1_g), .f(tarefa01_1_f), .a(tarefa01_1_a), .b(tarefa01_1_b), .e(tarefa01_1_e),
    .d(tarefa01_1_d), .c(tarefa01_1_c));  // open: dp
  _7_Segment_Display u_7_segment_display_2 (
    .g(tarefa01_1_g0), .f(tarefa01_1_f0), .a(tarefa01_1_a0), .b(tarefa01_1_b0), .e(tarefa01_1_e0),
    .d(tarefa01_1_d0), .c(tarefa01_1_c0));  // open: dp

  // Notes on the sheet:
  //   Entradas
  //   Unidade
  //   Dezena
endmodule

module _74185outro (
  input  S5,
  input  S4,
  input  S3,
  input  S2,
  input  S1,
  input  S0,
  output Y5,
  output Y4,
  output Y3,
  output Y2,
  output Y1,
  output Y0
);


  assign Y0 = S0;
  assign Y1 = S1;
  assign Y2 = S2;
  assign Y3 = S3;
  assign Y4 = S4;
  assign Y5 = S5;
endmodule
